# Fritzing sketch Schema (saved by Fritzing 0.9.3b)
breadboards: 1

parts:
  Part1 = Arduino Uno (Rev3)
  R6 = Resistor [tolerance=±5% resistance=220 package="0603 [SMD]"]
  R7 = Resistor [tolerance=±5% resistance=220 package="0603 [SMD]"]
  R8 = Resistor [tolerance=±5% resistance=220 package="0603 [SMD]"]
  Part2 = KY-009 Full Color RGB LED SMD Module [package="Breakout board"]

nets:
  N1: Part1.D9_PWM, R6.Pin_0
  N2: Part1.D10_PWM/SS, R8.Pin_0
  N3: Part1.D11_PWM/MOSI, R7.Pin_0
  N4: Part1.GND, Part2.-
  N5: R6.Pin_1, Part2.B
  N6: R7.Pin_1, Part2.G
  N7: R8.Pin_1, Part2.R

custom parts:
  KY-009 Full Color RGB LED SMD Module: RGB full color LED Module KY-009 for Arduino, emits a range of colors by mixing red, green and blue. The amount of each primary color is adjusted using PWM.
